# Fritzing sketch robot_schematic (saved by Fritzing 0.9.3b)

parts:
  S3 = H-Bridge with L298N
  M1 = DC Motor
  M4 = DC Motor
  Raspberry_Pi_1 = Raspberry Pi 4 [part_number=RPI-4-b]
  M5 = DC Motor
  M6 = DC Motor
  M7 = DC Motor
  M8 = DC Motor
  USBTTL1 = USB A Plug  # not connected
  USBTTL2 = Micro USB B Plug
  BATT2 = LiPoly Battery (1300mAh)
  U1 = LM2596 step down module

nets:
  N1: S3.12V, BATT2.positive, U1.IN+
  GND: S3.GND, Raspberry_Pi_1.GND, USBTTL2.usb, BATT2.negative, U1.IN-, U1.OUT+, U1.OUT-
  N2: S3.ENA, S3.ENA-5V
  N3: S3.IN1, Raspberry_Pi_1.GPIO23
  N4: S3.IN2, Raspberry_Pi_1.GPIO24
  N5: S3.IN3, Raspberry_Pi_1.GPIO25
  N6: S3.IN4, Raspberry_Pi_1.GPIO12
  N7: S3.ENB, S3.ENB-5V
  N8: S3.M1-01, M1.pin_2, M7.pin_2, M8.pin_2
  N9: S3.M1-02, M1.pin_1, M7.pin_1, M8.pin_1
  N10: S3.M2-01, M4.pin_2, M5.pin_2, M6.pin_2
  N11: S3.M2-02, M4.pin_1, M5.pin_1, M6.pin_1

notes:
  Step Down DC-DC 5V
  Battery Li-Po 7.4V
  Kamera Razer Kiyo
  Raspberry Pi 4B
  Motor DC Driver L298N
  6 x Motor DC
  Intel Neural Compute Stick 2

custom parts:
  H-Bridge with L298N: h-bridge
  Raspberry Pi 4: The RPi4, a faster version of the awesome Raspberry Pi 2 B ARM Board with 40 pin gpio. Ready for special Raspberry Pi B+ and RPi2 Hat (Hardware attached (on) top)
  LiPoly Battery (1300mAh): Lithium Ion Polymer Battery (1300mAh)
  LM2596 step down module: LM2596 DC-DC step down power supply module 3 A.
